# Fritzing sketch skematik aja wemos_smart hirdoponik_blynk (saved by Fritzing 0.9.3b)

parts:
  Part1 = Adafruit ADS1115 16Bit I2C ADC [part_number="Adafruit #1085"]
  WeMos_D1_R1 = WeMos D1 R2
  KY-1 = Keyes Relay [package=THT]
  KY-2 = Keyes Relay [package=THT]
  KY-3 = Keyes Relay [package=THT]
  KY-4 = Keyes Relay [package=THT]
  S1 = PH meter [package=THT]
  YF-S201_Flow_Meter1 = YF-S201 Water Flow Meter
  LCD3 = LCD screen
  YF-S201_Flow_Meter3 = YF-S201 Water Flow Meter
  YF-S201_Flow_Meter4 = YF-S201 Water Flow Meter
  YF-S201_Flow_Meter5 = YF-S201 Water Flow Meter
  U1 = LM2596 step down module
  LCM1602_IIC1 = LCM1602 IIC [part_number="LCM1602 IIC" chip_label="LCM1602 IIC" package="DIP (Dual Inline) [THT]"]
  S2 = PH meter [package=THT]
  M1 = DC Motor
  M2 = DC Motor
  M3 = DC Motor
  M4 = DC Motor
  R1 = Resistor [tolerance=±5% resistance=220 package=THT]
  R2 = Resistor [tolerance=±5% resistance=220 package=THT]
  PS1 = prefix0000 [part_number=S-350-60]

nets:
  N1: Part1.AIN1, S2.pin1
  N2: Part1.AIN0, S1.pin1
  N3: Part1.ADDR, Part1.SDA, WeMos_D1_R1.D4, R1.Pin_0
  N4: Part1.SCL, R2.Pin_0
  GND: Part1.GND, WeMos_D1_R1.GND#21, S1.pin3, LCM1602_IIC1.GND, S2.pin3
  VDD: Part1.VDD, WeMos_D1_R1.5V, S1.pin2, LCM1602_IIC1.VCC
  N5: WeMos_D1_R1.D0/RX, KY-1.signal
  N6: WeMos_D1_R1.D1/TX, KY-3.signal
  N7: WeMos_D1_R1.D2, KY-2.signal
  N8: WeMos_D1_R1.(D5), KY-4.signal
  N9: WeMos_D1_R1.(D6), YF-S201_Flow_Meter5.SIG
  N10: WeMos_D1_R1.(D7), YF-S201_Flow_Meter3.SIG
  N11: WeMos_D1_R1.D8, YF-S201_Flow_Meter4.SIG
  N12: WeMos_D1_R1.D9, YF-S201_Flow_Meter1.SIG
  N13: WeMos_D1_R1.GND#20, KY-1.ground
  N14: KY-1.NC, KY-2.NC, KY-3.NC, KY-4.NC
  N15: KY-1.C, M2.pin_2
  N16: KY-2.C, M4.pin_2
  N17: KY-3.C, M3.pin_2
  N18: KY-4.ground, U1.IN-, U1.OUT-, PS1.connector4
  N19: KY-4.C, M1.pin_2
  VSS: LCD3.VSS, LCM1602_IIC1.VSS
  VDD_2: LCD3.VDD, LCM1602_IIC1.VDD
  N20: LCD3.V0, LCM1602_IIC1.V0
  N21: LCD3.RS, LCM1602_IIC1.RS
  N22: LCD3.R/W, LCM1602_IIC1.RW
  N23: LCD3.E, LCM1602_IIC1.E
  N24: LCD3.DB0, LCM1602_IIC1.D0
  N25: LCD3.DB1, LCM1602_IIC1.D1
  N26: LCD3.DB2, LCM1602_IIC1.D2
  N27: LCD3.DB3, LCM1602_IIC1.D3
  N28: LCD3.DB4, LCM1602_IIC1.D4
  N29: LCD3.DB5, LCM1602_IIC1.D5
  N30: LCD3.DB6, LCM1602_IIC1.D6
  N31: LCD3.DB7, LCM1602_IIC1.D7
  N32: LCD3.LED+, LCM1602_IIC1.A
  N33: LCD3.LED-, LCM1602_IIC1.K
  N34: YF-S201_Flow_Meter5.VCC, U1.OUT+
  N35: U1.IN+, PS1.connector2
  N36: LCM1602_IIC1.SDA, R1.Pin_1
  N37: LCM1602_IIC1.SCL, R2.Pin_1
  N38: LCM1602_IIC1.LED_A, LCM1602_IIC1.LED_B

notes:
  Ke PLN

custom parts:
  Adafruit ADS1115 16Bit I2C ADC: For microcontrollers without an analog-to-digital converter or when you want a higher-precision ADC, the ADS1115 provides 16-bit precision at 860 samples/second over I2C. The chip can be configured as 4 single-ended input channels, or two differential channels. As a nice bonus, it even includes a programmable gain amplifier, up to x16, to help boost up smaller single/differential signals to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
  WeMos D1 R2: The D1 R2 is a mini wifi board based on the ESP-8266EX.
  Keyes Relay: The Keyes 5V relay module is suitable for SCM development, home appliance control. It uses a 5V~12V TIL control signal which can control DC / AC signal.
  YF-S201 Water Flow Meter: The YF-S201 Flow Meter. The input voltage is 5V to 24V (DC).
  LM2596 step down module: LM2596 DC-DC step down power supply module 3 A.
  LCM1602 IIC: I2C-Module to use a 1602 or 2004 LCD on with the wire.h libory Serial LCD Modul
